# Fritzing sketch NotGate (saved by Fritzing 0.9.9b)
circuit board: 3.60683cm x 2.2891cm
breadboards: 1

parts:
  Q = NPN-Transistor [package="TO92 [THT]"]
  RIN = Resistor [tolerance=±5% power=0.25 resistance=10k package=THT]
  OUT = female pin header, 1 pin [form="♀ (female)"]
  IN = female pin header, 1 pin [form="♀ (female)"]
  RVCC = Resistor [tolerance=±5% power=0.25 resistance=4.7k package=THT]
  VCC = female pin header, 1 pin [form="♀ (female)"]
  GND = female pin header, 1 pin [form="♀ (female)"]

nets (from the pcb view):
  N1: Q.E, OUT.pin1, RVCC.Pin_1
  N2: Q.B, RIN.Pin_0
  N3: Q.C, GND.pin1
  N4: RIN.Pin_1, IN.pin1
  N5: RVCC.Pin_0, VCC.pin1
