# Fritzing sketch AndGate (saved by Fritzing 0.9.9b)
circuit board: 3.55125cm x 3.94139cm
breadboards: 1

parts:
  Q1 = NPN-Transistor [package="TO92 [THT]"]
  Q2 = NPN-Transistor [package="TO92 [THT]"]
  R1 = Resistor [tolerance=±5% power=0.25 resistance=10k package=THT]
  R2 = Resistor [tolerance=±5% power=0.2 resistance=10k package=THT]
  R3 = Resistor [tolerance=±5% power=0.25W resistance=4.7k package=THT]
  B = female pin header, 1 pin [form="♀ (female)"]
  A = female pin header, 1 pin [form="♀ (female)"]
  OUT = female pin header, 1 pin [form="♀ (female)"]
  VCC = female pin header, 1 pin [form="♀ (female)"]
  GND = female pin header, 1 pin [form="♀ (female)"]

nets:
  N1: Q1.E, VCC.pin1
  N2: Q1.B, R1.Pin_1
  N3: Q1.C, Q2.E
  N4: Q2.B, R2.Pin_1
  N5: Q2.C, R3.Pin_0, OUT.pin1
  N6: R1.Pin_0, B.pin1
  N7: R2.Pin_0, A.pin1
  N8: R3.Pin_1, GND.pin1

notes:
  AND GATE
