# Fritzing sketch OrGate (saved by Fritzing 0.9.9b)
circuit board: 4.05765cm x 3.37157cm
breadboards: 1

parts:
  QA = NPN-Transistor [package="TO92 [THT]"]
  QB = NPN-Transistor [package="TO92 [THT]"]
  RB = Resistor [tolerance=±5% power=0.25 resistance=10k package=THT]
  RA = Resistor [tolerance=±5% power=0.25 resistance=10k package=THT]
  GND = female pin header, 1 pin [form="♀ (female)"]
  A = female pin header, 1 pin [form="♀ (female)"]
  B = female pin header, 1 pin [form="♀ (female)"]
  VCC = female pin header, 1 pin [form="♀ (female)"]
  RVCC = Resistor [tolerance=±5% power=0.25 resistance=4.7k package=THT]
  OUT = female pin header, 1 pin [form="♀ (female)"]

nets (from the pcb view):
  N1: QA.E, QB.E, GND.pin1
  N2: QA.B, RA.Pin_0
  N3: QA.C, QB.C, RVCC.Pin_1, OUT.pin1
  N4: QB.B, RB.Pin_0
  N5: RB.Pin_1, B.pin1
  N6: RA.Pin_1, A.pin1
  N7: VCC.pin1, RVCC.Pin_0
